// Logisim project tinycpu.circ as structural Verilog: 2 circuits, main circuit main
module main (
  input  in_1,
  input  DFF_D1,
  input  ADD_C1,
  input  DFF_D2,
  input  S,
  input  ADD_A1,
  input  in_7,
  input  in_8,
  input  ADD_B1,
  input  R,
  input  in_11,
  input  in_12,
  input  in_13,
  input  DFF_EN,
  input  D,
  input  EN,
  input  in_17,
  input  in_18,
  input  [7:0] in_19,
  input  in_20,
  input  in_21,
  input  in_22,
  input  [7:0] in_23,
  input  in_24,
  input  ram_we,
  input  MUX1_SEL,
  input  MUX_A,
  input  MUX_B,
  input  MUX_C,
  input  MUX_D,
  input  mux_a2,
  input  mux_b2,
  input  mux_c2,
  input  mux_d2,
  input  [1:0] MUX_SEL,
  output [2:0] out_36,
  output [7:0] out_37,
  output [7:0] out_38
);

  wire and_1_out, and_2_out, and_3_out, and_4_out, and_5_out, and_6_out, and_7_out, and_8_out, and_9_out,
       and_10_out, and_11_out, and_12_out, and_13_out, and_14_out, and_15_out, and_16_out, and_17_out,
       and_18_out, and_19_out, and_20_out, and_21_out, and_22_out, and_23_out, and_24_out, and_25_out,
       and_26_out, and_27_out, and_28_out, and_29_out, clock_1_out, clock_2_out, decoder_1_out0,
       decoder_1_out1, DFF_clk_out, nor_3_out, nor_4_out, nor_5_out, nor_6_out, nor_7_out, nor_8_out,
       nor_9_out, nor_10_out, not_1_out, not_2_out, not_3_out, not_4_out, not_5_out, not_6_out, not_7_out,
       not_8_out, not_9_out, not_10_out, not_11_out, not_12_out, or_1_out, or_2_out, or_3_out, or_4_out,
       or_5_out, or_6_out, or_7_out, or_8_out, or_9_out, or_10_out, or_11_out, SUM_x_out, SUM_y_out,
       undriven, xor_1_out, xor_2_out, xor_3_out;
  wire [3:0] REG_MAR;
  wire [7:0] multiplexer_1_out, RAM1, undriven_2, undriven_3;

  not not_1 (not_1_out, D);
  not not_2 (not_2_out, MUX1_SEL);
  not not_3 (not_3_out, MUX1_SEL);
  nor nor_1 (in_1, S, in_13);
  nor nor_2 (in_13, in_1, R);
  and and_1 (and_1_out, D, EN);
  and and_2 (and_2_out, in_17, not_2_out);
  and and_3 (and_3_out, in_21, MUX1_SEL);
  and and_4 (and_4_out, in_18, not_3_out);
  and and_5 (and_5_out, in_22, MUX1_SEL);
  and and_6 (and_6_out, not_1_out, EN);
  not not_4 (not_4_out, MUX_SEL[0]);
  nor nor_3 (nor_3_out, and_1_out, nor_4_out);
  nor nor_4 (nor_4_out, nor_3_out, and_6_out);
  or or_1 (or_1_out, and_2_out, and_3_out);
  or or_2 (or_2_out, and_4_out, and_5_out);
  not not_5 (not_5_out, MUX_SEL[0]);
  not not_6 (not_6_out, MUX_SEL[0]);
  not not_7 (not_7_out, MUX_SEL[0]);
  and and_7 (and_7_out, mux_a2, not_4_out);
  and and_8 (and_8_out, mux_b2, MUX_SEL[0]);
  and and_9 (and_9_out, mux_c2, not_7_out);
  and and_10 (and_10_out, mux_d2, MUX_SEL[0]);
  and and_11 (and_11_out, MUX_A, not_5_out);
  and and_12 (and_12_out, MUX_B, MUX_SEL[0]);
  and and_13 (and_13_out, MUX_C, not_6_out);
  and and_14 (and_14_out, MUX_D, MUX_SEL[0]);
  or or_3 (or_3_out, and_11_out, and_12_out);
  or or_4 (or_4_out, and_7_out, and_8_out);
  or or_5 (or_5_out, and_9_out, and_10_out);
  Clock DFF_clk (.out(DFF_clk_out));
  or or_6 (or_6_out, and_13_out, and_14_out);
  not not_8 (not_8_out, MUX_SEL[1]);
  and and_15 (and_15_out, DFF_clk_out, DFF_EN);
  not not_9 (not_9_out, MUX_SEL[1]);
  and and_16 (and_16_out, or_4_out, not_8_out);
  and and_17 (and_17_out, or_5_out, MUX_SEL[1]);
  and and_18 (and_18_out, or_3_out, not_9_out);
  and and_19 (and_19_out, or_6_out, MUX_SEL[1]);
  or or_7 (or_7_out, and_16_out, and_17_out);
  not not_10 (not_10_out, DFF_D2);
  Register register_1 (.D(in_19), .en(in_20), .clk(clock_1_out), .Q(out_37));  // open: clr
  Clock clock_1 (.out(clock_1_out));
  Register register_2 (.D(in_23), .en(in_24), .clk(clock_2_out), .Q(out_38));  // open: clr
  Clock clock_2 (.out(clock_2_out));
  or or_8 (or_8_out, and_18_out, and_19_out);
  not not_11 (not_11_out, DFF_D1);
  and and_20 (and_20_out, DFF_D2, and_15_out);
  and and_21 (and_21_out, DFF_D1, and_15_out);
  and and_22 (and_22_out, not_11_out, and_15_out);
  not not_12 (not_12_out, DFF_clk_out);
  and and_23 (and_23_out, not_10_out, and_15_out);
  Register #(.width(4)) mem_addr_register (.en(undriven), .Q(REG_MAR));  // open: D, clk, clr
  nor nor_5 (nor_5_out, and_21_out, nor_6_out);
  nor nor_6 (nor_6_out, nor_5_out, and_22_out);
  nor nor_7 (nor_7_out, and_20_out, nor_8_out);
  nor nor_8 (nor_8_out, nor_7_out, and_23_out);
  and and_24 (and_24_out, nor_5_out, not_12_out);
  and and_25 (and_25_out, nor_6_out, not_12_out);
  Decoder #(.select(4)) decoder_1 (
    .out0(decoder_1_out0), .out1(decoder_1_out1), .sel(REG_MAR), .en(ram_we));  // open: out2, out3, out4, out5, out6, out7, out8, out9, out10, out11, out12, out13, out14, out15
  nor nor_9 (nor_9_out, and_24_out, nor_10_out);
  nor nor_10 (nor_10_out, nor_9_out, and_25_out);
  Register register_3 (.D(undriven_2), .en(decoder_1_out0), .Q(RAM1));  // open: clk, clr
  Register register_4 (.en(decoder_1_out1));  // open: D, clk, Q, clr
  Register register_5 ();  // open: D, en, clk, Q, clr
  Register register_6 ();  // open: D, en, clk, Q, clr
  Register register_7 (.D(undriven_3));  // open: en, clk, Q, clr
  Register register_8 ();  // open: D, en, clk, Q, clr
  Register register_9 ();  // open: D, en, clk, Q, clr
  Register register_10 ();  // open: D, en, clk, Q, clr
  xor xor_1 (xor_1_out, ADD_A1, ADD_B1);
  xor xor_2 (xor_2_out, in_7, in_11);
  xor xor_3 (xor_3_out, in_8, in_12);
  Register register_11 ();  // open: D, en, clk, Q, clr
  Register register_12 ();  // open: D, en, clk, Q, clr
  Register register_13 ();  // open: D, en, clk, Q, clr
  Register register_14 ();  // open: D, en, clk, Q, clr
  xor SUM_i (out_36[0], xor_1_out, ADD_C1);
  and SUM_y (SUM_y_out, xor_1_out, ADD_C1);
  and SUM_x (SUM_x_out, ADD_A1, ADD_B1);
  and and_26 (and_26_out, xor_2_out, or_9_out);
  and and_27 (and_27_out, in_7, in_11);
  and and_28 (and_28_out, xor_3_out, or_10_out);
  and and_29 (and_29_out, in_8, in_12);
  xor xor_4 (out_36[1], xor_2_out, or_9_out);
  xor xor_5 (out_36[2], xor_3_out, or_10_out);
  or or_9 (or_9_out, SUM_y_out, SUM_x_out);
  or or_10 (or_10_out, and_26_out, and_27_out);
  or or_11 (or_11_out, and_28_out, and_29_out);
  Register register_15 ();  // open: D, en, clk, Q, clr
  Register register_16 ();  // open: D, en, clk, Q, clr
  Register register_17 ();  // open: D, en, clk, Q, clr
  Register register_18 ();  // open: D, en, clk, Q, clr
  Multiplexer #(.select(4), .width(8)) multiplexer_1 (
    .in0(RAM1), .out(multiplexer_1_out), .sel(REG_MAR));  // open: in1, in2, in3, in4, in5, in6, in7, in8, in9, in10, in11, in12, in13, in14, in15
endmodule

module cpu (
  input  in_1,
  input  in_2,
  input  in_3,
  input  in_4,
  input  in_5,
  input  in_6,
  input  in_7,
  input  [2:0] REG_SEL,
  input  REG_MANUAL_SEL,
  input  [7:0] MANUAL_DATA,
  input  in_11,
  input  in_12,
  input  in_13,
  input  [3:0] in_14,
  output [7:0] out_15,
  output [7:0] out_16,
  output [7:0] out_17,
  output [7:0] out_18,
  output [3:0] out_19,
  output [7:0] out_20,
  output [7:0] out_21,
  output [7:0] out_22,
  output [7:0] out_23,
  output [7:0] out_24,
  output [7:0] out_25,
  output [7:0] out_26,
  output [7:0] out_27,
  output [7:0] out_28,
  output [7:0] out_29,
  output [7:0] out_30,
  output [7:0] out_31,
  output [7:0] out_32,
  output [7:0] out_33,
  output [7:0] out_34,
  output [7:0] out_35,
  output [7:0] out_36,
  output [7:0] out_37,
  output [11:0] out_38,
  output [7:0] out_39,
  output [7:0] out_40,
  output [7:0] out_41,
  output [7:0] out_42
);

  wire CLK, clock_2_out, ram_we1, ram_we2, ram_we3, ram_we4, ram_we5, ram_we6, ram_we7, ram_we8, ram_we9,
       ram_we10, ram_we11, ram_we12, ram_we13, ram_we14, ram_we15, ram_we16;
  wire [3:0] INSTR_STEP_NEXT, PC_NEXT, REG_PC;
  wire [7:0] REG_MUX;

  Clock clock_1 (.out(CLK));
  Register REG_A (.D(out_15), .en(out_38[11]), .clk(CLK), .Q(out_16));  // open: clr
  Register REG_B (.D(out_15), .en(out_38[10]), .clk(CLK), .Q(out_17));  // open: clr
  Register REG_C (.D(out_15), .en(out_38[9]), .clk(CLK), .Q(out_18));  // open: clr
  Register #(.width(4)) REG_MAR (.D(out_15[3:0]), .en(out_38[8]), .clk(CLK), .Q(out_19));  // open: clr
  Register REG_INST (.D(out_15), .en(out_38[5]), .clk(CLK), .Q(out_23));  // open: clr
  Register #(.width(4)) register_1 (.D(PC_NEXT), .en(out_38[6]), .clk(CLK), .Q(REG_PC), .clr(in_11));
  Register #(.width(4)) register_2 (.D(INSTR_STEP_NEXT), .en(1'b1), .clk(CLK), .Q(out_40[3:0]), .clr(in_13));
  Adder adder_1 (.a(out_16), .b(out_17), .out(out_20), .cin(1'b0));  // open: cout
  ROM #(.dataWidth(12)) rom_1 (.addr({out_23[7:4], out_40[3:0]}), .data(out_38));
  Adder #(.width(4)) adder_2 (.a(REG_PC), .b(4'b0001), .out(PC_NEXT));  // open: cin, cout
  assign out_22 = {{4{1'b0}}, REG_PC};  // Bit_Extender bit_extender_1
  Multiplexer #(.select(3), .width(8)) multiplexer_1 (
    .in0(out_16), .in1(out_17), .in2(out_18), .in3(out_20), .in4(out_21), .in5(out_22), .in6(out_23),
    .out(REG_MUX), .sel(out_38[4:2]));  // open: in7
  RAM #(.addrWidth(4), .asyncread("true"), .\type ("nonvolatile")) ram_1 (
    .addr(out_19), .we(out_38[7]), .oe(in_12), .clk(CLK), .dout(out_21));  // open: din
  Adder #(.width(4)) adder_3 (.a(out_40[3:0]), .b(4'b0001), .out(INSTR_STEP_NEXT));  // open: cin, cout
  Multiplexer #(.width(8)) multiplexer_2 (.in0(REG_MUX), .in1(MANUAL_DATA), .out(out_15), .sel(REG_MANUAL_SEL));
  Decoder #(.select(4)) decoder_1 (
    .out0(ram_we1), .out1(ram_we2), .out2(ram_we3), .out3(ram_we4), .out4(ram_we5), .out5(ram_we6),
    .out6(ram_we7), .out7(ram_we8), .out8(ram_we9), .out9(ram_we10), .out10(ram_we11), .out11(ram_we12),
    .out12(ram_we13), .out13(ram_we14), .out14(ram_we15), .out15(ram_we16), .sel(out_19), .en(out_38[7]));
  RAM #(.addrWidth(4), .trigger("falling"), .\type ("nonvolatile")) ram_2 (
    .addr(in_14), .we(1'b0), .oe(1'b1), .clk(clock_2_out), .dout(out_24));  // open: din
  Clock clock_2 (.out(clock_2_out));
  Register register_3 (.D(out_15), .en(ram_we1), .clk(CLK), .Q(out_25));  // open: clr
  Register register_4 (.D(out_15), .en(ram_we2), .clk(CLK), .Q(out_26));  // open: clr
  Register register_5 (.D(out_15), .en(ram_we3), .clk(CLK), .Q(out_27));  // open: clr
  Register register_6 (.D(out_15), .en(ram_we4), .clk(CLK), .Q(out_28));  // open: clr
  Register register_7 (.D(out_15), .en(ram_we5), .clk(CLK), .Q(out_29));  // open: clr
  Register register_8 (.D(out_15), .en(ram_we6), .clk(CLK), .Q(out_30));  // open: clr
  Register register_9 (.D(out_15), .en(ram_we7), .clk(CLK), .Q(out_31));  // open: clr
  Register register_10 (.D(out_15), .en(ram_we8), .clk(CLK), .Q(out_32));  // open: clr
  Register register_11 (.D(out_15), .en(ram_we9), .clk(CLK), .Q(out_33));  // open: clr
  Register register_12 (.D(out_15), .en(ram_we10), .clk(CLK), .Q(out_34));  // open: clr
  Register register_13 (.D(out_15), .en(ram_we11), .clk(CLK), .Q(out_35));  // open: clr
  Register register_14 (.D(out_15), .en(ram_we12), .clk(CLK), .Q(out_36));  // open: clr
  Register register_15 (.D(out_15), .en(ram_we13), .clk(CLK), .Q(out_37));  // open: clr
  Register register_16 (.D(out_15), .en(ram_we14), .clk(CLK), .Q(out_39));  // open: clr
  Register register_17 (.D(out_15), .en(ram_we15), .clk(CLK), .Q(out_41));  // open: clr
  Register register_18 (.D(out_15), .en(ram_we16), .clk(CLK), .Q(out_42));  // open: clr
  Multiplexer #(.select(4), .width(8)) multiplexer_3 (
    .in0(out_25), .in1(out_26), .in2(out_27), .in3(out_28), .in4(out_29), .in5(out_30), .in6(out_31),
    .in7(out_32), .in8(out_33), .in9(out_34), .in10(out_35), .in11(out_36), .in12(out_37), .in13(out_39),
    .in14(out_41), .in15(out_42), .sel(out_19));  // open: out

  assign out_40[7:4] = out_23[7:4];

  // Other names for the same wires on the sheet: ALU_OUT[7:0] = out_20; CONTROL_FLAGS[11:0] = out_38;
  //   INST_WE = out_38[5]; PC_WE = out_38[6]; RAM_WE = out_38[7]; MAR_WE = out_38[8]; C_WE = out_38[9];
  //   B_WE = out_38[10]; A_WE = out_38[11]; INSTR_STEP_RESET = in_13; PC_CLR = in_11; RAM1[7:0] = out_25;
  //   RAM2[7:0] = out_26; RAM3[7:0] = out_27; RAM4[7:0] = out_28; RAM5[7:0] = out_29; RAM6[7:0] = out_30;
  //   RAM7[7:0] = out_31; RAM8[7:0] = out_32; RAM9[7:0] = out_33; RAM10[7:0] = out_34; RAM11[7:0] = out_35;
  //   RAM12[7:0] = out_36; RAM13[7:0] = out_37; RAM14[7:0] = out_39; RAM15[7:0] = out_41; RAM16[7:0] = out_42;
  //   REG_A[7:0] = out_16; REG_B[7:0] = out_17; REG_C[7:0] = out_18; INST_ADDR[3:0] = out_23[3:0];
  //   REG_INST[7:0] = out_23; REG_MAR[3:0] = out_19; REG_PC_EXT[7:0] = out_22; REG_RAM[7:0] = out_21;
  //   REG_SEL_t[2:0] = out_38[4:2]; INSTR_LOOKUP[7:0] = {out_23[7:4], out_40[3:0]}; INSTR_STEP[3:0] = out_40[3:0];
  //   ROM_LOOKUP[7:0] = {out_23[7:4], out_40[3:0]}; INST_OPCODE[3:0] = out_23[7:4]; BUS_4_LSB[3:0] = out_15[3:0];
  //   THE_BUS[7:0] = out_15; BUS_4_MSB[3:0] = out_15[7:4]

  // Notes on the sheet:
  //   a = 0, b = 1, c = 2, alu = 3, ram = 4, pc = 5, inst=6
  //   contents of rom_1 (hex, n*v repeats v):
  //   114 70 14*0 114 70 118 810 12*0 114 70 14*0 114 70 14*0 114 70 14*0 114 70 14*0 114 70 14*0 114 70
  //   14*0 114 70 14*0 114 70 14*0 114 70 14*0 114 70 14*0 114 70 14*0 114 70 14*0 114 70 14*0 114 70
endmodule
